// Logisim project SynthBite16.circ as structural Verilog: 1 circuit, main circuit main
module main (
);

  wire MasterClock_out;

  Clock MasterClock (.out(MasterClock_out));
  // Shift_Register #(.length(16)) Accumulator: pin names not known
endmodule
